# Fritzing sketch intval2 (saved by Fritzing 0.9.2b)
breadboards: 1

parts:
  Part1 = Pro Trinket 5V
  S1 = H-Bridge with L298N
  JACK1 = 2.1mm Barrel Jack with Terminal Block

nets:
  GND: Part1.GND, S1.GND, JACK1.POS
  N1: Part1.VBAT, S1.5V
  N2: S1.12V, JACK1.NEG
  N3: S1.M1-02, S1.M2-01, S1.M2-02

custom parts:
  Pro Trinket 5V: The Pro Trinket 5V is like an Arduino Pro Mini with more pins and USB included. Built with the common core Arduino chip, the ATmega328p, it has 18 GPIO, 2 extra analog inputs, 28K of flash, and 2K of RAM. It has onboard USB bootloading support with Optiboot support, so you can either program your Pro Trinket over USB or with a FTDI cable. The Pro Trinket is programmable using the Arduino IDE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
  H-Bridge with L298N: h-bridge
